// Digital circuit sapALU_1.dig as structural Verilog
module sapALU_1 (
  input  INV,
  input  CY,
  input  [7:0] A,
  input  [7:0] B,
  input  SUB
);

  wire or_1_out, or_2_out, sapalu0_1_cy_ou, sapalu0_2_cy_ou, sapalu0_3_cy_ou, sapalu0_4_cy_ou,
       sapalu0_5_cy_ou, sapalu0_6_cy_ou, sapalu0_7_cy_ou;
  wire [3:0] sapalu0_1_s, sapalu0_5_s;

  or or_1 (or_1_out, SUB, INV);
  or or_2 (or_2_out, CY, SUB);
  sapALU0 sapalu0_1 (.CY_in(or_2_out), .A(A[0]), .B(B[0]), .INV(or_1_out), .S(sapalu0_1_s[0]), .CY_ou(sapalu0_1_cy_ou));
  sapALU0 sapalu0_2 (
    .CY_in(sapalu0_1_cy_ou), .A(A[1]), .B(B[1]), .INV(or_1_out), .S(sapalu0_1_s[1]), .CY_ou(sapalu0_2_cy_ou));
  sapALU0 sapalu0_3 (
    .CY_in(sapalu0_2_cy_ou), .A(A[2]), .B(B[2]), .INV(or_1_out), .S(sapalu0_1_s[2]), .CY_ou(sapalu0_3_cy_ou));
  sapALU0 sapalu0_4 (
    .CY_in(sapalu0_3_cy_ou), .A(A[3]), .B(B[3]), .INV(or_1_out), .S(sapalu0_1_s[3]), .CY_ou(sapalu0_4_cy_ou));
  sapALU0 sapalu0_5 (
    .CY_in(sapalu0_4_cy_ou), .A(A[4]), .B(B[4]), .INV(or_1_out), .S(sapalu0_5_s[0]), .CY_ou(sapalu0_5_cy_ou));
  sapALU0 sapalu0_6 (
    .CY_in(sapalu0_5_cy_ou), .A(A[5]), .B(B[5]), .INV(or_1_out), .S(sapalu0_5_s[1]), .CY_ou(sapalu0_6_cy_ou));
  sapALU0 sapalu0_7 (
    .CY_in(sapalu0_6_cy_ou), .A(A[6]), .B(B[6]), .INV(or_1_out), .S(sapalu0_5_s[2]), .CY_ou(sapalu0_7_cy_ou));
  sapALU0 sapalu0_8 (.CY_in(sapalu0_7_cy_ou), .A(A[7]), .B(B[7]), .INV(or_1_out), .S(sapalu0_5_s[3]));  // open: CY_ou
  Seven_Seg_Hex seven_seg_hex_1 (.d(A[3:0]), .dp(1'b0));
  Seven_Seg_Hex seven_seg_hex_2 (.d(A[7:4]), .dp(1'b0));
  Seven_Seg_Hex seven_seg_hex_3 (.d(sapalu0_1_s), .dp(1'b0));
  Seven_Seg_Hex seven_seg_hex_4 (.d(sapalu0_5_s), .dp(1'b0));
  Seven_Seg_Hex seven_seg_hex_5 (.d(B[3:0]), .dp(1'b0));
  Seven_Seg_Hex seven_seg_hex_6 (.d(B[7:4]), .dp(1'b0));

  // Other names for the same wires on the sheet: RA[7:0] = A; RB[7:0] = B
endmodule
